# Fritzing sketch Buzzer & LED & Photocell (saved by Fritzing 0.9.4)
breadboards: 1

parts:
  Part1 = Arduino Uno (Rev3)
  J1 = Piezo Speaker
  R1 = PHOTOCELL [package=photocell-kit]
  R2 = Resistor [tolerance=±5% resistance=10k package=THT]
  LED1 = LED - 5mm [color="Red (633nm)" package="5 mm [THT]"]

nets:
  N1: Part1.A0, R1.P$1, R2.Pin_1
  N2: Part1.D8, J1.pin2
  N3: Part1.D9_PWM, LED1.anode
  N4: Part1.5V, R1.P$2
  N5: Part1.GND, J1.pin1, R2.Pin_0, LED1.cathode
